# Fritzing sketch HC05-FastLeds-Basic (saved by Fritzing 0.9.3b)

parts:
  Part1 = Arduino Uno (Rev3)
  Part2 = Bluetooth HC-05 Macho
  Part3 = Arduino Nano (Rev3.0)
  NEOPIXEL1 = WS2812b strip
  J1 = Camdenboss CTB0158-2 [part_number=CTB0158-2 package=THT]

nets:
  N1: Part1.A4/SDA, Part3.A4
  N2: Part1.A5/SCL, Part3.A5
  N3: Part1.D2, Part2.TXD
  N4: Part1.D3_PWM, Part2.RXD
  3V3: Part1.3V3, Part2.VCC
  N5: Part1.5V, J1.terminal_2
  GND: Part1.GND, Part2.GND, J1.terminal_1
  N6: Part3.D6, NEOPIXEL1.+5V
  GND_2: Part3.GND, NEOPIXEL1.GND, J1.pin1
  N7: Part3.5V, NEOPIXEL1.DI, J1.pin2

custom parts:
  WS2812b strip: ws2812b strip.
