# Fritzing sketch HC05-FastLeds-adv (saved by Fritzing 0.9.3b)
circuit board: 8.46667cm x 5.64444cm

parts:
  Part1 = Arduino Uno (Rev3)
  Part2 = Bluetooth HC-05 Macho
  Part3 = Arduino Nano (Rev3.0)
  NEOPIXEL1 = WS2812b strip  # not connected
  Part5 = Arduino Ethernet Shield (Rev3)
  J1 = Power Jack [package=power_jack_smd]
  J2 = Camdenboss CTB0158-2 [part_number=CTB0158-2 package=THT]
  S1 = Toggle Switch [package=THT]
  S2 = Toggle Switch [package=THT]

nets:
  N1: Part1.A5/SCL, Part3.A5
  N2: Part1.D8, Part2.TXD
  N3: Part1.D9_PWM, Part2.RXD
  N4: Part1.A4/SDA, Part3.A4
  N5: Part1.5V, J2.terminal_1
  N6: Part1.GND, J2.terminal_2
  VCC: Part2.VCC, Part5.3V3
  GND: Part2.GND, Part5.GND
  N7: J1.PWR, J2.pin1
  N8: J1.GND, J2.pin2
  N9: S1.COM, S2.COM
  N10: S1.L2, S2.L2

notes:
  I2C
  RS485
  HC05
  Uno Below

custom parts:
  WS2812b strip: ws2812b strip.
